// Logisim project DEMUX14.circ as structural Verilog: 1 circuit, main circuit main
module main (
  input  A,
  input  S_1,
  input  A_2,
  input  S_0,
  input  S_1_2,
  input  A_3,
  input  A_4,
  input  S_1_3,
  input  S_1_4,
  input  S_0_2,
  input  A_5,
  input  S_1_5,
  input  S_0_3,
  output Z0,
  output z0_2,
  output Z1,
  output z1_2,
  output Z2,
  output Z3,
  output z0_3,
  output Z0_4,
  output z1_3,
  output Z1_4,
  output Z2_2,
  output Z3_2,
  output Z0_5,
  output Z1_5,
  output Z2_3,
  output Z3_3
);

  wire _3_2_out, _3_3_out, _3_4_out, _3_5_out, _3_6_out, _3_out, _4_out, nand_1_out, nand_2_out, nand_3_out,
       nand_4_out, nand_5_out, nand_6_out, nand_7_out, nand_8_out, nand_9_out, not_1_out, not_2_out,
       not_3_out, not_4_out, not_5_out, not_6_out, not_7_out, not_12_out;

  not not_1 (not_1_out, S_1);
  and _3 (_3_out, not_1_out, not_2_out);
  not not_2 (not_2_out, S_0);
  not not_3 (not_3_out, S_1);
  and _3_2 (_3_2_out, not_3_out, S_0);
  and _3_3 (_3_3_out, S_1, not_4_out);
  not not_4 (not_4_out, S_0);
  and _3_4 (_3_4_out, S_1, S_0);
  nand nand_1 (nand_1_out, S_1_3, S_0_2);
  nand nand_2 (nand_2_out, A_5, S_1_5);
  not not_5 (not_5_out, nand_2_out);
  nor _4 (_4_out, S_1_3, S_0_2);
  and _3_5 (_3_5_out, S_0_2, nand_1_out);
  and _3_6 (_3_6_out, S_1_3, nand_1_out);
  not not_6 (not_6_out, nand_1_out);
  not not_7 (not_7_out, nand_3_out);
  nand nand_3 (nand_3_out, A_5, nand_2_out);
  and _3_7 (Z0, A, _3_out);
  and _3_8 (Z1, A, _3_2_out);
  and _3_9 (Z2, A, _3_3_out);
  and _3_10 (Z3, A, _3_4_out);
  and _3_11 (Z0_4, A_4, _4_out);
  and _3_12 (Z1_4, A_4, _3_5_out);
  and _3_13 (Z2_2, A_4, _3_6_out);
  and _3_14 (Z3_2, A_4, not_6_out);
  nand nand_4 (nand_4_out, not_7_out, S_0_3);
  nand nand_5 (nand_5_out, not_5_out, S_0_3);
  nand nand_6 (nand_6_out, not_7_out, nand_4_out);
  not not_8 (Z1_5, nand_4_out);
  nand nand_7 (nand_7_out, not_5_out, nand_5_out);
  not not_9 (Z3_3, nand_5_out);
  not not_10 (Z0_5, nand_6_out);
  not not_11 (Z2_3, nand_7_out);
  not not_12 (not_12_out, S_1_2);
  nand nand_8 (nand_8_out, A_3, S_1_4);
  and and_1 (z0_2, not_12_out, A_2, A_2);
  and and_2 (z1_2, S_1_2, A_2);
  not not_13 (z1_3, nand_8_out);
  nand nand_9 (nand_9_out, A_3, nand_8_out);
  not not_14 (z0_3, nand_9_out);

  // Notes on the sheet:
  //   NANDs: 20
  //   NANDs: 18
  //   NANDs: 12 (optimal)
  //   DEMUX12 template
  //   DEMUX12 template (optimized)
endmodule
