// Logisim project DEMUX41.circ as structural Verilog: 1 circuit, main circuit main
module main (
  input  in_1,
  input  in_2,
  input  in_3,
  input  A,
  input  S_1,
  input  S_0,
  output out_7,
  output out_8,
  output out_9,
  output out_10
);

  wire and_1_out, and_2_out, and_3_out, and_4_out, and_5_out, and_6_out, and_7_out, and_8_out, and_9_out,
       and_10_out, nand_1_out, nor_1_out, not_1_out, not_2_out, not_3_out, not_4_out, not_5_out;

  not not_1 (not_1_out, in_2);
  not not_2 (not_2_out, in_3);
  not not_3 (not_3_out, in_2);
  not not_4 (not_4_out, in_3);
  and and_1 (and_1_out, not_1_out, not_2_out);
  and and_2 (and_2_out, not_3_out, in_3);
  and and_3 (and_3_out, in_2, not_4_out);
  and and_4 (and_4_out, in_2, in_3);
  nand nand_1 (nand_1_out, S_1, S_0);
  nor nor_1 (nor_1_out, S_1, S_0);
  and and_5 (and_5_out, S_1, nand_1_out);
  and and_6 (and_6_out, S_0, nand_1_out);
  not not_5 (not_5_out, nand_1_out);
  and and_7 (and_7_out, in_1, and_1_out);
  and and_8 (and_8_out, in_1, and_2_out);
  and and_9 (and_9_out, in_1, and_3_out);
  and and_10 (and_10_out, in_1, and_4_out);
  and and_11 (out_7, A, nor_1_out);
  and and_12 (out_8, A, and_5_out);
  and and_13 (out_9, A, and_6_out);
  and and_14 (out_10, A, not_5_out);

  // Notes on the sheet:
  //   NANDs: 20
  //   NANDs: 18
endmodule
