// Logisim project MUX41.circ as structural Verilog: 1 circuit, main circuit main
module main (
  input  in_1,
  input  S,
  input  in_3,
  input  I1,
  input  I2,
  input  I3
);

  wire nand_1_out, nand_2_out, nand_3_out, nand_4_out, nand_5_out, nand_6_out, nand_7_out, nand_8_out,
       nand_9_out, nand_10_out, nand_11_out, not_1_out, not_2_out, not_3_out, not_4_out, not_5_out,
       not_6_out, not_7_out, not_8_out, not_9_out, not_10_out;

  not not_1 (not_1_out, in_1);
  not not_2 (not_2_out, S);
  not not_3 (not_3_out, S);
  not not_4 (not_4_out, S);
  nand nand_1 (nand_1_out, not_1_out, not_2_out);
  not not_5 (not_5_out, nand_1_out);
  not not_6 (not_6_out, nand_2_out);
  nand nand_2 (nand_2_out, not_3_out, S);
  nand nand_3 (nand_3_out, in_1, not_4_out);
  not not_7 (not_7_out, nand_3_out);
  not not_8 (not_8_out, nand_4_out);
  nand nand_4 (nand_4_out, in_1, S);
  nand nand_5 (nand_5_out, not_5_out, in_3);
  nand nand_6 (nand_6_out, not_6_out, I1);
  nand nand_7 (nand_7_out, not_7_out, I2);
  nand nand_8 (nand_8_out, nand_5_out, nand_6_out);
  nand nand_9 (nand_9_out, nand_7_out, nand_10_out);
  nand nand_10 (nand_10_out, not_8_out, I3);
  not not_9 (not_9_out, nand_8_out);
  not not_10 (not_10_out, nand_9_out);
  nand nand_11 (nand_11_out, not_9_out, not_10_out);

  // Notes on the sheet:
  //   JI
  //   J
  //   K
  //   L
  //   M
  //   I0
  //   KI
  //   LI
  //   MI
  //   Z
endmodule
