// Logisim project MUX81X8.circ as structural Verilog: 1 circuit, main circuit main
module main (
  output out_1,
  output out_2,
  output out_3,
  output out_4,
  output out_5,
  output out_6,
  output out_7,
  output out_8
);

  wire and_1_out, and_2_out, and_3_out, and_4_out, and_5_out, and_6_out, and_7_out, and_8_out, and_9_out,
       and_10_out, and_11_out, and_12_out, and_13_out, and_14_out, and_15_out, and_16_out, and_17_out,
       and_18_out, and_19_out, and_20_out, and_21_out, and_22_out, and_23_out, and_24_out, and_25_out,
       and_26_out, and_27_out, and_28_out, and_29_out, and_30_out, and_31_out, and_32_out, and_33_out,
       and_34_out, and_35_out, and_36_out, and_37_out, and_38_out, and_39_out, and_40_out, and_41_out,
       and_42_out, and_43_out, and_44_out, and_45_out, and_46_out, and_47_out, and_48_out, and_49_out,
       and_50_out, and_51_out, and_52_out, and_53_out, and_54_out, and_55_out, and_56_out, and_57_out,
       and_58_out, and_59_out, and_60_out, and_61_out, and_62_out, and_63_out, and_64_out, and_65_out,
       and_66_out, and_67_out, and_68_out, and_69_out, and_70_out, and_71_out, and_72_out, and_73_out,
       and_74_out, and_75_out, and_76_out, and_77_out, and_78_out, and_79_out, and_80_out, and_81_out,
       and_82_out, and_83_out, and_84_out, and_85_out, and_86_out, and_87_out, and_88_out, and_89_out,
       and_90_out, and_91_out, and_92_out, and_93_out, and_94_out, and_95_out, and_96_out, and_97_out,
       and_98_out, and_99_out, and_100_out, and_101_out, and_102_out, and_103_out, and_104_out, and_105_out,
       and_106_out, and_107_out, and_108_out, and_109_out, and_110_out, and_111_out, and_112_out,
       and_113_out, and_114_out, and_115_out, and_116_out, and_117_out, and_118_out, and_119_out,
       and_120_out, and_121_out, and_122_out, and_123_out, and_124_out, and_125_out, and_126_out,
       and_127_out, and_128_out, clock_1_out, not_1_out, not_2_out, not_3_out, not_4_out, not_5_out,
       not_6_out, not_7_out, not_8_out, not_9_out, not_10_out, not_11_out, not_12_out, not_13_out,
       not_14_out, not_15_out, not_16_out, not_17_out, not_18_out, not_19_out, not_20_out, not_21_out,
       not_22_out, not_23_out, not_24_out, not_25_out, not_26_out, not_27_out, not_28_out, not_29_out,
       not_30_out, not_31_out, not_32_out, not_33_out, not_34_out, not_35_out, not_36_out, not_37_out,
       not_38_out, not_39_out, not_40_out, not_41_out, not_42_out, not_43_out, not_44_out, not_45_out,
       not_46_out, not_47_out, not_48_out, not_49_out, not_50_out, not_51_out, not_52_out, not_53_out,
       not_54_out, not_55_out, not_56_out, not_57_out, not_58_out, not_59_out, not_60_out, not_61_out,
       not_62_out, not_63_out, not_64_out, not_65_out, not_66_out, not_67_out, not_68_out, not_69_out,
       not_70_out, not_71_out, not_72_out, not_73_out, not_74_out, not_75_out, not_76_out, not_77_out,
       not_78_out, not_79_out, not_80_out, not_81_out, not_82_out, not_83_out, not_84_out, not_85_out,
       not_86_out, not_87_out, not_88_out, not_89_out, not_90_out, not_91_out, not_92_out, not_93_out,
       not_94_out, not_95_out, not_96_out;
  wire [2:0] random_9_out;
  wire [7:0] random_1_out, random_2_out, random_3_out, random_4_out, random_5_out, random_6_out,
       random_7_out, random_8_out;

  Clock clock_1 (.out(clock_1_out));
  Random random_1 (.clk(clock_1_out), .out(random_1_out));  // open: next, clr
  Random random_2 (.clk(clock_1_out), .out(random_2_out));  // open: next, clr
  Random random_3 (.clk(clock_1_out), .out(random_3_out));  // open: next, clr
  Random random_4 (.clk(clock_1_out), .out(random_4_out));  // open: next, clr
  Random random_5 (.clk(clock_1_out), .out(random_5_out));  // open: next, clr
  Random #(.seed(2)) random_6 (.clk(clock_1_out), .out(random_6_out));  // open: next, clr
  Random random_7 (.clk(clock_1_out), .out(random_7_out));  // open: next, clr
  Random random_8 (.clk(clock_1_out), .out(random_8_out));  // open: next, clr
  Random #(.width(3)) random_9 (.clk(clock_1_out), .out(random_9_out));  // open: next, clr
  not not_1 (not_1_out, random_9_out[0]);
  not not_2 (not_2_out, random_9_out[1]);
  not not_3 (not_3_out, random_9_out[2]);
  not not_4 (not_4_out, random_9_out[0]);
  not not_5 (not_5_out, random_9_out[1]);
  not not_6 (not_6_out, random_9_out[0]);
  not not_7 (not_7_out, random_9_out[2]);
  not not_8 (not_8_out, random_9_out[0]);
  not not_9 (not_9_out, random_9_out[1]);
  not not_10 (not_10_out, random_9_out[2]);
  not not_11 (not_11_out, random_9_out[1]);
  not not_12 (not_12_out, random_9_out[2]);
  not not_13 (not_13_out, random_9_out[0]);
  not not_14 (not_14_out, random_9_out[1]);
  not not_15 (not_15_out, random_9_out[2]);
  not not_16 (not_16_out, random_9_out[0]);
  not not_17 (not_17_out, random_9_out[1]);
  not not_18 (not_18_out, random_9_out[0]);
  not not_19 (not_19_out, random_9_out[2]);
  not not_20 (not_20_out, random_9_out[0]);
  not not_21 (not_21_out, random_9_out[1]);
  not not_22 (not_22_out, random_9_out[2]);
  not not_23 (not_23_out, random_9_out[1]);
  not not_24 (not_24_out, random_9_out[2]);
  and and_1 (and_1_out, not_1_out, not_2_out, not_3_out);
  and and_2 (and_2_out, not_4_out, not_5_out, random_9_out[2]);
  and and_3 (and_3_out, not_6_out, random_9_out[1], not_7_out);
  and and_4 (and_4_out, not_8_out, random_9_out[1], random_9_out[2]);
  and and_5 (and_5_out, random_9_out[0], not_9_out, not_10_out);
  and and_6 (and_6_out, random_9_out[0], not_11_out, random_9_out[2]);
  and and_7 (and_7_out, random_9_out[0], random_9_out[1], not_12_out);
  and and_8 (and_8_out, random_9_out[0], random_9_out[1], random_9_out[2]);
  and and_9 (and_9_out, not_13_out, not_14_out, not_15_out);
  and and_10 (and_10_out, not_16_out, not_17_out, random_9_out[2]);
  and and_11 (and_11_out, not_18_out, random_9_out[1], not_19_out);
  and and_12 (and_12_out, not_20_out, random_9_out[1], random_9_out[2]);
  and and_13 (and_13_out, random_9_out[0], not_21_out, not_22_out);
  and and_14 (and_14_out, random_9_out[0], not_23_out, random_9_out[2]);
  and and_15 (and_15_out, random_9_out[0], random_9_out[1], not_24_out);
  and and_16 (and_16_out, random_9_out[0], random_9_out[1], random_9_out[2]);
  and and_17 (and_17_out, and_1_out, random_8_out[0]);
  and and_18 (and_18_out, and_2_out, random_7_out[0]);
  and and_19 (and_19_out, and_9_out, random_8_out[1]);
  and and_20 (and_20_out, and_10_out, random_7_out[1]);
  and and_21 (and_21_out, and_3_out, random_6_out[0]);
  and and_22 (and_22_out, and_11_out, random_6_out[1]);
  and and_23 (and_23_out, and_4_out, random_5_out[0]);
  and and_24 (and_24_out, and_12_out, random_5_out[1]);
  and and_25 (and_25_out, and_5_out, random_4_out[0]);
  and and_26 (and_26_out, and_6_out, random_3_out[0]);
  and and_27 (and_27_out, and_13_out, random_4_out[1]);
  and and_28 (and_28_out, and_14_out, random_3_out[1]);
  and and_29 (and_29_out, and_7_out, random_2_out[0]);
  and and_30 (and_30_out, and_15_out, random_2_out[1]);
  and and_31 (and_31_out, and_8_out, random_1_out[0]);
  and and_32 (and_32_out, and_16_out, random_1_out[1]);
  or or_1 (out_1, and_17_out, and_18_out, and_21_out, and_23_out, and_25_out, and_26_out, and_29_out, and_31_out);
  or or_2 (out_2, and_19_out, and_20_out, and_22_out, and_24_out, and_27_out, and_28_out, and_30_out, and_32_out);
  not not_25 (not_25_out, random_9_out[0]);
  not not_26 (not_26_out, random_9_out[1]);
  not not_27 (not_27_out, random_9_out[2]);
  not not_28 (not_28_out, random_9_out[0]);
  not not_29 (not_29_out, random_9_out[1]);
  not not_30 (not_30_out, random_9_out[0]);
  not not_31 (not_31_out, random_9_out[2]);
  not not_32 (not_32_out, random_9_out[0]);
  not not_33 (not_33_out, random_9_out[1]);
  not not_34 (not_34_out, random_9_out[2]);
  not not_35 (not_35_out, random_9_out[1]);
  not not_36 (not_36_out, random_9_out[2]);
  not not_37 (not_37_out, random_9_out[0]);
  not not_38 (not_38_out, random_9_out[1]);
  not not_39 (not_39_out, random_9_out[2]);
  not not_40 (not_40_out, random_9_out[0]);
  not not_41 (not_41_out, random_9_out[1]);
  not not_42 (not_42_out, random_9_out[0]);
  not not_43 (not_43_out, random_9_out[2]);
  not not_44 (not_44_out, random_9_out[0]);
  not not_45 (not_45_out, random_9_out[1]);
  not not_46 (not_46_out, random_9_out[2]);
  not not_47 (not_47_out, random_9_out[1]);
  not not_48 (not_48_out, random_9_out[2]);
  and and_33 (and_33_out, not_25_out, not_26_out, not_27_out);
  and and_34 (and_34_out, not_28_out, not_29_out, random_9_out[2]);
  and and_35 (and_35_out, not_30_out, random_9_out[1], not_31_out);
  and and_36 (and_36_out, not_32_out, random_9_out[1], random_9_out[2]);
  and and_37 (and_37_out, random_9_out[0], not_33_out, not_34_out);
  and and_38 (and_38_out, random_9_out[0], not_35_out, random_9_out[2]);
  and and_39 (and_39_out, random_9_out[0], random_9_out[1], not_36_out);
  and and_40 (and_40_out, random_9_out[0], random_9_out[1], random_9_out[2]);
  and and_41 (and_41_out, not_37_out, not_38_out, not_39_out);
  and and_42 (and_42_out, not_40_out, not_41_out, random_9_out[2]);
  and and_43 (and_43_out, not_42_out, random_9_out[1], not_43_out);
  and and_44 (and_44_out, not_44_out, random_9_out[1], random_9_out[2]);
  and and_45 (and_45_out, random_9_out[0], not_45_out, not_46_out);
  and and_46 (and_46_out, random_9_out[0], not_47_out, random_9_out[2]);
  and and_47 (and_47_out, random_9_out[0], random_9_out[1], not_48_out);
  and and_48 (and_48_out, random_9_out[0], random_9_out[1], random_9_out[2]);
  and and_49 (and_49_out, and_33_out, random_8_out[2]);
  and and_50 (and_50_out, and_34_out, random_7_out[2]);
  and and_51 (and_51_out, and_41_out, random_8_out[3]);
  and and_52 (and_52_out, and_42_out, random_7_out[3]);
  and and_53 (and_53_out, and_35_out, random_6_out[2]);
  and and_54 (and_54_out, and_43_out, random_6_out[3]);
  and and_55 (and_55_out, and_36_out, random_5_out[2]);
  and and_56 (and_56_out, and_44_out, random_5_out[3]);
  and and_57 (and_57_out, and_37_out, random_4_out[2]);
  and and_58 (and_58_out, and_38_out, random_3_out[2]);
  and and_59 (and_59_out, and_45_out, random_4_out[3]);
  and and_60 (and_60_out, and_46_out, random_3_out[3]);
  and and_61 (and_61_out, and_39_out, random_2_out[2]);
  and and_62 (and_62_out, and_47_out, random_2_out[3]);
  and and_63 (and_63_out, and_40_out, random_1_out[2]);
  and and_64 (and_64_out, and_48_out, random_1_out[3]);
  or or_3 (out_3, and_49_out, and_50_out, and_53_out, and_55_out, and_57_out, and_58_out, and_61_out, and_63_out);
  or or_4 (out_4, and_51_out, and_52_out, and_54_out, and_56_out, and_59_out, and_60_out, and_62_out, and_64_out);
  not not_49 (not_49_out, random_9_out[0]);
  not not_50 (not_50_out, random_9_out[1]);
  not not_51 (not_51_out, random_9_out[2]);
  not not_52 (not_52_out, random_9_out[0]);
  not not_53 (not_53_out, random_9_out[1]);
  not not_54 (not_54_out, random_9_out[0]);
  not not_55 (not_55_out, random_9_out[2]);
  not not_56 (not_56_out, random_9_out[0]);
  not not_57 (not_57_out, random_9_out[1]);
  not not_58 (not_58_out, random_9_out[2]);
  not not_59 (not_59_out, random_9_out[1]);
  not not_60 (not_60_out, random_9_out[2]);
  not not_61 (not_61_out, random_9_out[0]);
  not not_62 (not_62_out, random_9_out[1]);
  not not_63 (not_63_out, random_9_out[2]);
  not not_64 (not_64_out, random_9_out[0]);
  not not_65 (not_65_out, random_9_out[1]);
  not not_66 (not_66_out, random_9_out[0]);
  not not_67 (not_67_out, random_9_out[2]);
  not not_68 (not_68_out, random_9_out[0]);
  not not_69 (not_69_out, random_9_out[1]);
  not not_70 (not_70_out, random_9_out[2]);
  not not_71 (not_71_out, random_9_out[1]);
  not not_72 (not_72_out, random_9_out[2]);
  and and_65 (and_65_out, not_49_out, not_50_out, not_51_out);
  and and_66 (and_66_out, not_52_out, not_53_out, random_9_out[2]);
  and and_67 (and_67_out, not_54_out, random_9_out[1], not_55_out);
  and and_68 (and_68_out, not_56_out, random_9_out[1], random_9_out[2]);
  and and_69 (and_69_out, random_9_out[0], not_57_out, not_58_out);
  and and_70 (and_70_out, random_9_out[0], not_59_out, random_9_out[2]);
  and and_71 (and_71_out, random_9_out[0], random_9_out[1], not_60_out);
  and and_72 (and_72_out, random_9_out[0], random_9_out[1], random_9_out[2]);
  and and_73 (and_73_out, not_61_out, not_62_out, not_63_out);
  and and_74 (and_74_out, not_64_out, not_65_out, random_9_out[2]);
  and and_75 (and_75_out, not_66_out, random_9_out[1], not_67_out);
  and and_76 (and_76_out, not_68_out, random_9_out[1], random_9_out[2]);
  and and_77 (and_77_out, random_9_out[0], not_69_out, not_70_out);
  and and_78 (and_78_out, random_9_out[0], not_71_out, random_9_out[2]);
  and and_79 (and_79_out, random_9_out[0], random_9_out[1], not_72_out);
  and and_80 (and_80_out, random_9_out[0], random_9_out[1], random_9_out[2]);
  and and_81 (and_81_out, and_65_out, random_8_out[4]);
  and and_82 (and_82_out, and_66_out, random_7_out[4]);
  and and_83 (and_83_out, and_73_out, random_8_out[5]);
  and and_84 (and_84_out, and_74_out, random_7_out[5]);
  and and_85 (and_85_out, and_67_out, random_6_out[4]);
  and and_86 (and_86_out, and_75_out, random_6_out[5]);
  and and_87 (and_87_out, and_68_out, random_5_out[4]);
  and and_88 (and_88_out, and_76_out, random_5_out[5]);
  and and_89 (and_89_out, and_69_out, random_4_out[4]);
  and and_90 (and_90_out, and_70_out, random_3_out[4]);
  and and_91 (and_91_out, and_77_out, random_4_out[5]);
  and and_92 (and_92_out, and_78_out, random_3_out[5]);
  and and_93 (and_93_out, and_71_out, random_2_out[4]);
  and and_94 (and_94_out, and_79_out, random_2_out[5]);
  and and_95 (and_95_out, and_72_out, random_1_out[4]);
  and and_96 (and_96_out, and_80_out, random_1_out[5]);
  or or_5 (out_5, and_81_out, and_82_out, and_85_out, and_87_out, and_89_out, and_90_out, and_93_out, and_95_out);
  or or_6 (out_6, and_83_out, and_84_out, and_86_out, and_88_out, and_91_out, and_92_out, and_94_out, and_96_out);
  not not_73 (not_73_out, random_9_out[0]);
  not not_74 (not_74_out, random_9_out[1]);
  not not_75 (not_75_out, random_9_out[2]);
  not not_76 (not_76_out, random_9_out[0]);
  not not_77 (not_77_out, random_9_out[1]);
  not not_78 (not_78_out, random_9_out[0]);
  not not_79 (not_79_out, random_9_out[2]);
  not not_80 (not_80_out, random_9_out[0]);
  not not_81 (not_81_out, random_9_out[1]);
  not not_82 (not_82_out, random_9_out[2]);
  not not_83 (not_83_out, random_9_out[1]);
  not not_84 (not_84_out, random_9_out[2]);
  not not_85 (not_85_out, random_9_out[0]);
  not not_86 (not_86_out, random_9_out[1]);
  not not_87 (not_87_out, random_9_out[2]);
  not not_88 (not_88_out, random_9_out[0]);
  not not_89 (not_89_out, random_9_out[1]);
  not not_90 (not_90_out, random_9_out[0]);
  not not_91 (not_91_out, random_9_out[2]);
  not not_92 (not_92_out, random_9_out[0]);
  not not_93 (not_93_out, random_9_out[1]);
  not not_94 (not_94_out, random_9_out[2]);
  not not_95 (not_95_out, random_9_out[1]);
  not not_96 (not_96_out, random_9_out[2]);
  and and_97 (and_97_out, not_73_out, not_74_out, not_75_out);
  and and_98 (and_98_out, not_76_out, not_77_out, random_9_out[2]);
  and and_99 (and_99_out, not_78_out, random_9_out[1], not_79_out);
  and and_100 (and_100_out, not_80_out, random_9_out[1], random_9_out[2]);
  and and_101 (and_101_out, random_9_out[0], not_81_out, not_82_out);
  and and_102 (and_102_out, random_9_out[0], not_83_out, random_9_out[2]);
  and and_103 (and_103_out, random_9_out[0], random_9_out[1], not_84_out);
  and and_104 (and_104_out, random_9_out[0], random_9_out[1], random_9_out[2]);
  and and_105 (and_105_out, not_85_out, not_86_out, not_87_out);
  and and_106 (and_106_out, not_88_out, not_89_out, random_9_out[2]);
  and and_107 (and_107_out, not_90_out, random_9_out[1], not_91_out);
  and and_108 (and_108_out, not_92_out, random_9_out[1], random_9_out[2]);
  and and_109 (and_109_out, random_9_out[0], not_93_out, not_94_out);
  and and_110 (and_110_out, random_9_out[0], not_95_out, random_9_out[2]);
  and and_111 (and_111_out, random_9_out[0], random_9_out[1], not_96_out);
  and and_112 (and_112_out, random_9_out[0], random_9_out[1], random_9_out[2]);
  and and_113 (and_113_out, and_97_out, random_8_out[6]);
  and and_114 (and_114_out, and_98_out, random_7_out[6]);
  and and_115 (and_115_out, and_105_out, random_8_out[7]);
  and and_116 (and_116_out, and_106_out, random_7_out[7]);
  and and_117 (and_117_out, and_99_out, random_6_out[6]);
  and and_118 (and_118_out, and_107_out, random_6_out[7]);
  and and_119 (and_119_out, and_100_out, random_5_out[6]);
  and and_120 (and_120_out, and_108_out, random_5_out[7]);
  and and_121 (and_121_out, and_101_out, random_4_out[6]);
  and and_122 (and_122_out, and_102_out, random_3_out[6]);
  and and_123 (and_123_out, and_109_out, random_4_out[7]);
  and and_124 (and_124_out, and_110_out, random_3_out[7]);
  and and_125 (and_125_out, and_103_out, random_2_out[6]);
  and and_126 (and_126_out, and_111_out, random_2_out[7]);
  and and_127 (and_127_out, and_104_out, random_1_out[6]);
  and and_128 (and_128_out, and_112_out, random_1_out[7]);
  or or_7 (out_7, and_113_out, and_114_out, and_117_out, and_119_out, and_121_out, and_122_out, and_125_out, and_127_out);
  or or_8 (out_8, and_115_out, and_116_out, and_118_out, and_120_out, and_123_out, and_124_out, and_126_out, and_128_out);

  // Notes on the sheet:
  //   JI
  //   J
  //   K
  //   L
  //   M
  //   N
  //   O
  //   P
  //   Q
  //   JI
  //   J
  //   K
  //   L
  //   M
  //   N
  //   O
  //   P
  //   Q
  //   KI
  //   KI
  //   LI
  //   LI
  //   MI
  //   NI
  //   MI
  //   NI
  //   OI
  //   OI
  //   PI
  //   PI
  //   QI
  //   QI
  //   JI
  //   J
  //   K
  //   L
  //   M
  //   N
  //   O
  //   P
  //   Q
  //   JI
  //   J
  //   K
  //   L
  //   M
  //   N
  //   O
  //   P
  //   Q
  //   KI
  //   KI
  //   LI
  //   LI
  //   MI
  //   NI
  //   MI
  //   NI
  //   OI
  //   OI
  //   PI
  //   PI
  //   QI
  //   QI
  //   JI
  //   J
  //   K
  //   L
  //   M
  //   N
  //   O
  //   P
  //   Q
  //   JI
  //   J
  //   K
  //   L
  //   M
  //   N
  //   O
  //   P
  //   Q
  //   KI
  //   KI
  //   LI
  //   LI
  //   MI
  //   NI
  //   MI
  //   NI
  //   OI
  //   OI
  //   PI
  //   PI
  //   QI
  //   QI
  //   JI
  //   J
  //   K
  //   L
  //   M
  //   N
  //   O
  //   P
  //   Q
  //   JI
  //   J
  //   K
  //   L
  //   M
  //   N
  //   O
  //   P
  //   Q
  //   KI
  //   KI
  //   LI
  //   LI
  //   MI
  //   NI
  //   MI
  //   NI
  //   OI
  //   OI
  //   PI
  //   PI
  //   QI
  //   QI
endmodule
