// Logisim project Truth_Table3_simplified.circ as structural Verilog: 1 circuit, main circuit main
module main (
  input  in_1,
  input  in_2,
  input  in_3,
  input  in_4
);

  wire nand_1_out, nand_2_out, nand_3_out, nand_4_out, nand_5_out, nand_6_out, nand_7_out, nor_1_out,
       not_1_out, not_2_out;

  not not_1 (not_1_out, in_3);
  not not_2 (not_2_out, in_4);
  nand nand_1 (nand_1_out, in_1, in_2);
  nand nand_2 (nand_2_out, in_1, not_2_out);
  nand nand_3 (nand_3_out, in_2, not_1_out);
  nand nand_4 (nand_4_out, in_2, not_2_out);
  nand nand_5 (nand_5_out, in_1, in_3);
  nand nand_6 (nand_6_out, nand_1_out, nand_2_out);
  nand nand_7 (nand_7_out, nand_3_out, nand_4_out);
  nor nor_1 (nor_1_out, nand_6_out, nand_7_out);
  // NAND_Gate nand_8 has open pins: in0=nor_1_out, in4=nand_5_out, out=open

  // Notes on the sheet:
  //   I
  //   J
  //   K
  //   L
  //   M
  //   N
  //   O
  //   P
  //   Z
endmodule
